# Fritzing sketch hardware (saved by Fritzing 0.8.7b)
breadboards: 1

parts:
  U1 = TLP621 [package=THT]
  U2 = TLP621 [package=THT]
  U3 = TLP621 [package=THT]
  U4 = TLP621 [package=THT]
  LED1 = LED - 5mm [color="Red (633nm)" package="5 mm [THT]"]
  LED2 = LED - 5mm [color="Red (633nm)" package="5 mm [THT]"]
  S1 = Pushbutton [package="[THT]"]
  S2 = Pushbutton [package="[THT]"]
  S3 = Pushbutton [package="[THT]"]
  S4 = Pushbutton [package="[THT]"]
  U5 = Spark Core (v1.0)
  T1 = TMP36 Temperature Sensor [package="TO92 [THT]"]

nets:
  N1: U1.Pin_1, U5.D3
  GND: U1.Pin_2, U2.Pin_2, U3.Pin_2, U4.Pin_2, LED1.cathode, LED2.cathode, U5.GND, T1.GND
  N2: U1.Pin_4, S3.Pin_1, S3.Pin_2
  N3: U1.Pin_3, S3.Pin_3, S3.Pin_4
  N4: U2.Pin_1, U5.D2
  N5: U2.Pin_4, S2.Pin_4
  N6: U2.Pin_3, S2.Pin_2
  N7: U3.Pin_1, U5.D1
  N8: U3.Pin_4, S1.Pin_1, S1.Pin_2
  N9: U3.Pin_3, S1.Pin_3, S1.Pin_4
  N10: U4.Pin_1, U5.D0
  N11: U4.Pin_4, S4.Pin_1, S4.Pin_2
  N12: U4.Pin_3, S4.Pin_3, S4.Pin_4
  N13: LED1.anode, U5.D4
  N14: LED2.anode, U5.D5
  N15: U5.A2, U5.3V3
  N16: U5.A3, U5.A6
  N17: U5.A5, U5.VIN
  N18: U5.A7, T1.Vout
  N19: U5.3V3*, T1.+Vs

notes:
  start
  lock
  unlock
  trunk

custom parts:
  Spark Core (v1.0): The Spark Core is a tiny Wi-Fi development board that makes it easy to create internet-connected hardware. The Core is all you need to get started; power it over USB and in minutes you'll be controlling LEDs, switches and motors and collecting data from sensors over the internet! It has 8 digital I/O pins, 8 analog I/O pins, 8 PWM pins; UART (Serial), SPI, I2C, and JTAG peripherals available.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
